# Fritzing sketch ESP32_PCB_A_001 (saved by Fritzing 0.9.3b)
stripboards: 1

parts:
  U1 = ESP32-38PinWide [part_number=ESP32-38PinWide]  # not connected
  o1 = Module display OLED I2C 128x64 SSD1306 [package=THT]  # not connected
  J1 = female pin header, 19 pins [form="♀ (female)"]
  J2 = female pin header, 19 pins [form="♀ (female)"]
  J11 = male pin header, 2 pins [form="♂ (male)"]
  J21 = male pin header, 3 pins [form="♂ (male)"]
  J22 = male pin header, 3 pins [form="♂ (male)"]
  J23 = male pin header, 3 pins [form="♂ (male)"]
  J24 = male pin header, 3 pins [form="♂ (male)"]
  J25 = male pin header, 3 pins [form="♂ (male)"]
  J26 = male pin header, 3 pins [form="♂ (male)"]
  S1 = Pushbutton [package=THT]
  S2 = Pushbutton [package=THT]
  S3 = Pushbutton [package=THT]
  S4 = Pushbutton [package=THT]
  LED2 = LED - 5mm [color="Red (633nm)" package="5 mm [THT]"]  # not connected
  LED3 = LED - 5mm [color="Green (570nm)" package="5 mm [THT]"]  # not connected
  LED4 = LED - 5mm [color="Blue (525nm)" package="5 mm [THT]"]  # not connected
  LED5 = LED - 5mm [color="White (4500K)" package="5 mm [THT]"]  # not connected
  R3 = Resistor [tolerance=±5% resistance=220 package=THT]
  R4 = Resistor [tolerance=±5% resistance=220 package=THT]
  R5 = Resistor [tolerance=±5% resistance=220 package=THT]
  R6 = Resistor [tolerance=±5% resistance=220 package=THT]
  J42 = male pin header, 19 pins [form="♂ (male)"]
  J44 = male pin header, 19 pins [form="♂ (male)"]
  J13 = female pin header, 8 pins [form="♀ (female)"]
  J14 = female pin header, 8 pins [form="♀ (female)"]
  J16 = male pin header, 8 pins [form="♂ (male)"]
  J15 = male pin header, 8 pins [form="♂ (male)"]
  RE1 = Rotary Encoder [package=THT]
  J19 = male pin header, 3 pins [form="♂ (male)"]
  J20 = male pin header, 2 pins [form="♂ (male)"]  # not connected
  J31 = male pin header, 2 pins [form="♂ (male)"]
  J27 = male pin header, 2 pins [form="♂ (male)"]
  J51 = male pin header, 2 pins [form="♂ (male)"]
  J52 = male pin header, 2 pins [form="♂ (male)"]
  J53 = male pin header, 2 pins [form="♂ (male)"]
  J54 = male pin header, 2 pins [form="♂ (male)"]
  J55 = male pin header, 2 pins [form="♂ (male)"]
  J56 = male pin header, 2 pins [form="♂ (male)"]
  J6 = male pin header, 5 pins [form="♂ (male)"]
  J57 = male pin header, 9 pins [form="♂ (male)"]
  J5 = male pin header, 5 pins [form="♂ (male)"]
  J4 = male pin header, 9 pins [form="♂ (male)"]
  J3 = male pin header, 2 pins [form="♂ (male)"]
  J58 = male pin header, 2 pins [form="♂ (male)"]
  J59 = male pin header, 2 pins [form="♂ (male)"]
  J60 = male pin header, 2 pins [form="♂ (male)"]
  J61 = male pin header, 2 pins [form="♂ (male)"]
  J62 = male pin header, 2 pins [form="♂ (male)"]
  J63 = male pin header, 2 pins [form="♂ (male)"]
  J64 = male pin header, 2 pins [form="♂ (male)"]
  J65 = male pin header, 2 pins [form="♂ (male)"]
  J66 = male pin header, 2 pins [form="♂ (male)"]
  J67 = male pin header, 2 pins [form="♂ (male)"]
  J68 = male pin header, 2 pins [form="♂ (male)"]
  J69 = male pin header, 2 pins [form="♂ (male)"]
  J70 = male pin header, 2 pins [form="♂ (male)"]
  J35 = male pin header, 1 pin [form="♂ (male)"]  # not connected
  J39 = male pin header, 1 pin [form="♂ (male)"]
  J45 = male pin header, 1 pin [form="♂ (male)"]  # not connected
  J46 = male pin header, 1 pin [form="♂ (male)"]
  J47 = male pin header, 1 pin [form="♂ (male)"]  # not connected
  J48 = male pin header, 1 pin [form="♂ (male)"]
  J49 = male pin header, 1 pin [form="♂ (male)"]  # not connected
  J50 = male pin header, 1 pin [form="♂ (male)"]
  R7 = Trimmer Potentiometer [maximum_resistance=10kΩ package=THT]  # not connected
  R8 = Trimmer Potentiometer [maximum_resistance=10kΩ package=THT]  # not connected
  J7 = male pin header, 12 pins [form="♂ (male)"]
  J8 = male pin header, 12 pins [form="♂ (male)"]
  J9 = male pin header, 12 pins [form="♂ (male)"]
  J10 = male pin header, 12 pins [form="♂ (male)"]
  J71 = male pin header, 2 pins [form="♂ (male)"]
  J72 = male pin header, 1 pin [form="♂ (male)"]
  J73 = male pin header, 1 pin [form="♂ (male)"]
  J74 = male pin header, 2 pins [form="♂ (male)"]

nets:
  N1: J1.pin1, J1.pin7, J2.pin14, J23.pin1, J23.pin2, J23.pin3, J42.pin1, J42.pin2, J42.pin3, J42.pin4, J42.pin5, J42.pin6, J42.pin7, J42.pin8, J42.pin9, J42.pin10, J42.pin11, J42.pin12, J42.pin13, J42.pin14, J42.pin15, J42.pin16, J42.pin17, J42.pin18, J42.pin19, J6.pin1, J6.pin2, J6.pin3, J6.pin4, J6.pin5, J57.pin1, J57.pin2, J57.pin3, J57.pin4, J57.pin5, J57.pin6, J57.pin7, J57.pin8, J57.pin9, J10.pin1, J10.pin2, J10.pin3, J10.pin4, J10.pin5, J10.pin6, J10.pin7, J10.pin8, J10.pin9, J10.pin10, J10.pin11, J10.pin12, J72.pin1
  N2: J1.pin2, J3.pin1, J3.pin2
  N3: J1.pin3, J59.pin1, J59.pin2
  N4: J1.pin4, J58.pin1, J58.pin2
  N5: J1.pin5, J60.pin1, J60.pin2
  N6: J1.pin6, J61.pin1, J61.pin2
  N7: J1.pin8, J62.pin1, J62.pin2
  N8: J1.pin9, J63.pin1, J63.pin2
  N9: J1.pin10, J64.pin1, J64.pin2
  N10: J1.pin11, J65.pin1, J65.pin2
  N11: J1.pin12, J66.pin1, J66.pin2
  N12: J1.pin13, J67.pin1, J67.pin2
  N13: J1.pin14, J68.pin1, J68.pin2
  N14: J1.pin15, J69.pin1, J69.pin2
  N15: J1.pin16, J70.pin1, J70.pin2
  N16: J2.pin1, J74.pin2
  N17: J2.pin2, J7.pin1, J8.pin1
  N18: J2.pin3, J7.pin2, J8.pin2
  N19: J2.pin4, J7.pin3, J8.pin3
  N20: J2.pin5, J7.pin4, J8.pin4
  N21: J2.pin6, J7.pin5, J8.pin5
  N22: J2.pin7, J7.pin6, J8.pin6
  N23: J2.pin8, J7.pin7, J8.pin7
  N24: J2.pin9, J7.pin8, J8.pin8
  N25: J2.pin10, J7.pin9, J8.pin9
  N26: J2.pin11, J7.pin10, J8.pin10
  N27: J2.pin12, J7.pin11, J8.pin11
  N28: J2.pin13, J7.pin12, J8.pin12
  N29: J2.pin15, J71.pin1, J71.pin2
  N30: J2.pin19, J11.pin1, J11.pin2
  N31: J21.pin1, J22.pin1
  N32: J21.pin2, J22.pin2
  N33: J21.pin3, J22.pin3
  N34: J24.pin1, J24.pin2, J24.pin3, J44.pin1, J44.pin2, J44.pin3, J44.pin4, J44.pin5, J44.pin6, J44.pin7, J44.pin8, J44.pin9, J44.pin10, J44.pin11, J44.pin12, J44.pin13, J44.pin14, J44.pin15, J44.pin16, J44.pin17, J44.pin18, J44.pin19, J5.pin1, J5.pin2, J5.pin3, J5.pin4, J5.pin5, J4.pin1, J4.pin2, J4.pin3, J4.pin4, J4.pin5, J4.pin6, J4.pin7, J4.pin8, J4.pin9, J9.pin1, J9.pin2, J9.pin3, J9.pin4, J9.pin5, J9.pin6, J9.pin7, J9.pin8, J9.pin9, J9.pin10, J9.pin11, J9.pin12, J73.pin1, J74.pin1
  N35: J25.pin1, J26.pin1
  N36: J25.pin2, J26.pin2
  N37: J25.pin3, J26.pin3
  N38: S1.leg0, J27.pin1, J27.pin2
  N39: S1.leg1, J31.pin1, J31.pin2
  N40: S2.leg0, J52.pin1, J52.pin2
  N41: S2.leg1, J51.pin1, J51.pin2
  N42: S3.leg0, J54.pin1, J54.pin2
  N43: S3.leg1, J53.pin1, J53.pin2
  N44: S4.leg0, J56.pin1, J56.pin2
  N45: S4.leg1, J55.pin1, J55.pin2
  N46: R3.Pin_1, J39.pin1
  N47: R4.Pin_1, J46.pin1
  N48: R5.Pin_1, J48.pin1
  N49: R6.Pin_1, J50.pin1
  N50: J13.pin1, J14.pin1, J16.pin1, J15.pin1
  N51: J13.pin2, J14.pin2, J16.pin2, J15.pin2
  N52: J13.pin3, J14.pin3, J16.pin3, J15.pin3
  N53: J13.pin4, J14.pin4, J16.pin4, J15.pin4
  N54: J13.pin5, J14.pin5, J16.pin5, J15.pin5
  N55: J13.pin6, J14.pin6, J16.pin6, J15.pin6
  N56: J13.pin7, J14.pin7, J16.pin7, J15.pin7
  N57: J13.pin8, J14.pin8, J16.pin8, J15.pin8
  N58: RE1.EncoderPinA, J19.pin3
  N59: RE1.EncoderPinC, J19.pin2
  N60: RE1.EncoderPinB, J19.pin1

custom parts:
  ESP32-38PinWide: Generic 38-Pin ESP32 with wide format (only access to one side of pins on a breadboard) based on Stephen Lilley's HiLetgo ESP-WROOM-32 ESP32 ESP-32S Development Board.
  Module display OLED I2C 128x64 SSD1306: Ecran OLED I2C SSD163 de 128x64 avec connexion I2C
