# Fritzing sketch ESP32_PCB_A_003_a (saved by Fritzing 0.9.3b)
stripboards: 1

parts:
  Q1 = Basic FET N-Channel [package="TO220 [THT]"]
  Q2 = Basic FET N-Channel [package="TO220 [THT]"]
  Q3 = Basic FET N-Channel [package="TO220 [THT]"]
  J1 = female pin header, 2 pins [form="♀ (female)"]
  Q4 = NPN-Transistor [package="TO92 [THT]"]
  Q5 = NPN-Transistor [package="TO92 [THT]"]
  Q6 = NPN-Transistor [package="TO92 [THT]"]
  J4 = male pin header, 1 pin [form="♂ (male)"]
  J5 = male pin header, 1 pin [form="♂ (male)"]
  R8 = Resistor [tolerance=±5% resistance=10k package=THT]
  R9 = Resistor [tolerance=±5% resistance=10k package=THT]
  R10 = Resistor [tolerance=±5% resistance=10k package=THT]
  R11 = Resistor [tolerance=±5% resistance=10k package=THT]
  J2 = male pin header, 1 pin [form="♂ (male)"]
  J3 = male pin header, 1 pin [form="♂ (male)"]
  J6 = male pin header, 1 pin [form="♂ (male)"]
  J7 = male pin header, 1 pin [form="♂ (male)"]
  R12 = Resistor [tolerance=±5% resistance=220 package=THT]
  R13 = Resistor [tolerance=±5% resistance=220 package=THT]

nets:
  N1: Q1.gate, Q5.C, R10.Pin_1
  N2: Q1.drain, J7.pin1
  GND: Q1.source, Q2.source, Q3.source, J1.pin2
  N3: Q2.gate, Q4.C, R8.Pin_1
  N4: Q2.drain, J2.pin1
  N5: Q3.gate, Q6.C, R12.Pin_1
  N6: Q3.drain, J5.pin1
  12V: J1.pin1, R8.Pin_0, R10.Pin_0, R12.Pin_0
  N7: Q4.E, J3.pin1
  N8: Q4.B, R9.Pin_1
  N9: Q5.E, J6.pin1
  N10: Q5.B, R11.Pin_1
  N11: Q6.E, J4.pin1
  N12: Q6.B, R13.Pin_1
  3.3V: R9.Pin_0, R11.Pin_0, R13.Pin_0
