# Fritzing sketch ESP32-Kontakt (saved by Fritzing 0.9.3b)

parts:
  U3 = ESP32-38PinWide [part_number=ESP32-38PinWide]
  Desk_light_button_1 = Pushbutton [package=THT]
  status_led = LED - 5mm [color="Green (570nm)" package="5 mm [THT]"]
  R2 = Resistor [tolerance=±5% resistance=220 package=THT]
  U4 = 4-Channel 5v Relay Shield [package=relay-4ch5v10a]
  Desk_light_button_2 = Pushbutton [package=THT]

nets:
  3.3V: U3.3.3, status_led.anode
  N1: U3.GPIO33, U4.IN4
  N2: U3.GPIO25, U4.IN3
  N3: U3.GPIO26, U4.IN2
  N4: U3.GPIO27, U4.IN1
  GND: U3.GND, Desk_light_button_1.leg0, U4.GND, Desk_light_button_2.leg0
  N5: U3.GPIO13, R2.Pin_1
  VIN: U3.VIN, U4.VCC
  N6: U3.GPIO0, Desk_light_button_2.leg1
  N7: U3.GPIO4, Desk_light_button_1.leg1
  N8: status_led.cathode, R2.Pin_0
  N9: U4.K1-On, U4.K2-Off

custom parts:
  ESP32-38PinWide: Generic 38-Pin ESP32 with wide format (only access to one side of pins on a breadboard) based on Stephen Lilley's HiLetgo ESP-WROOM-32 ESP32 ESP-32S Development Board.
  4-Channel 5v Relay Shield: 4 Channel 5v Relay Shield w. 2x SPD-06VDC-SD-C
