# Fritzing sketch ESP32-Kontakt_LED (saved by Fritzing 0.9.3b)

parts:
  U3 = ESP32-38PinWide [part_number=ESP32-38PinWide]
  Desk_light_button_1 = Pushbutton [package=THT]
  status_led = LED - 5mm [color="Green (570nm)" package="5 mm [THT]"]
  R2 = Resistor [tolerance=±5% resistance=220 package=THT]
  Desk_light_button_2 = Pushbutton [package=THT]
  R3 = Resistor [tolerance=±5% resistance=220 package=THT]
  RedLed = LED - 5mm [color="Red (633nm)" package="5 mm [THT]"]

nets (from the breadboard view):
  N1: U3.3.3, status_led.anode, RedLed.anode
  N2: U3.GPIO14, R3.Pin_1
  N3: U3.GPIO12, R2.Pin_1
  N4: U3.GND, Desk_light_button_1.leg0, Desk_light_button_2.leg0
  N5: U3.GPIO0, Desk_light_button_2.leg1
  N6: U3.GPIO4, Desk_light_button_1.leg1
  N7: status_led.cathode, R2.Pin_0
  N8: R3.Pin_0, RedLed.cathode

custom parts:
  ESP32-38PinWide: Generic 38-Pin ESP32 with wide format (only access to one side of pins on a breadboard) based on Stephen Lilley's HiLetgo ESP-WROOM-32 ESP32 ESP-32S Development Board.
