# Fritzing sketch ESP32-Kontakt_Relay (saved by Fritzing 0.9.3b)

parts:
  U3 = ESP32-38PinWide [part_number=ESP32-38PinWide]
  Pir = Pushbutton [package=THT]
  status_led = LED - 5mm [color="Green (570nm)" package="5 mm [THT]"]
  R2 = Resistor [tolerance=±5% resistance=220 package=THT]
  U4 = 4-Channel 5v Relay Shield [package=relay-4ch5v10a]
  Front_Door = Pushbutton [package=THT]
  R3 = Resistor [tolerance=±5% resistance=220 package=THT]
  RedLed = LED - 5mm [color="Red (633nm)" package="5 mm [THT]"]

nets:
  3.3V: U3.3.3, status_led.anode, RedLed.anode
  N1: U3.GPIO32, Pir.leg0
  N2: U3.GPIO33, Front_Door.leg0
  N3: U3.GPIO25, R3.Pin_1
  N4: U3.GPIO26, R2.Pin_1
  GND: U3.GND, Pir.leg1, U4.GND, Front_Door.leg1
  VIN: U3.VIN, U4.VCC
  N5: U3.GPIO4, U4.IN4
  N6: U3.GPIO16, U4.IN3
  N7: U3.GPIO17, U4.IN2
  N8: U3.GPIO5, U4.IN1
  N9: status_led.cathode, R2.Pin_0
  N10: U4.K1-On, U4.K2-Off
  N11: R3.Pin_0, RedLed.cathode

custom parts:
  ESP32-38PinWide: Generic 38-Pin ESP32 with wide format (only access to one side of pins on a breadboard) based on Stephen Lilley's HiLetgo ESP-WROOM-32 ESP32 ESP-32S Development Board.
  4-Channel 5v Relay Shield: 4 Channel 5v Relay Shield w. 2x SPD-06VDC-SD-C
